# Fritzing sketch pi_pollution_painter (saved by Fritzing 1.0.2b)
breadboards: 1

parts:
  MCU1 = Raspberry Pi Zero
  Part_2_Arduino = Arduino Pro Mini (5V)
  Part3 = Adafruit 4-channel I2C-safe Bi-directional Logic Level Converter [part_number="Adafruit #757"]
  DOTSTAR1 = DotStar Strip -- Black (60/m) [part_number=2239]
  S1 = Round Pushbutton
  BAT1 = Battery Holders [package=battery-aa]

nets:
  N1: MCU1.pin_1, MCU1.pin_17, Part3.LV, S1.leg1
  N2: MCU1.pin_2, MCU1.pin_4, Part_2_Arduino.RAW
  GND: MCU1.pin_6, MCU1.pin_9, MCU1.pin_14, MCU1.pin_20, MCU1.pin_25, MCU1.pin_30, MCU1.pin_34, MCU1.pin_39, Part_2_Arduino.GND, Part3.GND, DOTSTAR1.GND#3
  N3: MCU1.pin_8, Part3.A1
  N4: MCU1.pin_10, Part3.A2
  N5: MCU1.pin_31, S1.leg0
  N6: Part_2_Arduino.TXO, Part3.B2
  N7: Part_2_Arduino.VCC, Part3.HV
  N8: Part_2_Arduino.SCK, DOTSTAR1.CI
  N9: Part_2_Arduino.MOSI, DOTSTAR1.DI
  N10: Part_2_Arduino.RXI, Part3.B1
  N11: DOTSTAR1.GND#4, BAT1.-
  N12: DOTSTAR1.+5V, BAT1.+

custom parts:
  Adafruit 4-channel I2C-safe Bi-directional Logic Level Converter: Because the Arduino (and Basic Stamp) are 5V devices, and most modern sensors, displays, flash cards and modes are 3.3V-only, many makers find that they need to perform level shifting/conversion to protect the 3.3V device from 5V. We do have some other handy level shifters in the shop, from the DIP 74LVC245 to the fancy bi-directional TXB0108. However, neither of these are happy to work with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
  DotStar Strip -- Black (60/m): NeopixelDotStar Strip, Black, 60 pixels per meter.
